# Fritzing sketch control (saved by Fritzing 0.8.7b)
perfboards: 1

parts:
  DIN1 = DIN-5 jack (MIDI) [package=THT]
  J1 = Screw terminal - 2 pins [package=THT]
  Composant1 = Arduino Uno (Rev3) - ICSP
  C1 = Electrolytic Capacitor [capacitance=4.7mF voltage=10V package="200 mil [THT, electrolytic]"]
  IC1 = DS1307 [package=THT]
  XTAL1 = Crystal [frequency="16 Mhz" package=THT]
  BAT1 = Battery Holders [package=battcon_12mm]
  R1 = Resistor [tolerance=±5% resistance=2.2k package=THT]
  R2 = Resistor [tolerance=±5% resistance=2.2k package=THT]
  Q1 = Basic FET N-Channel [package="TO220 [THT]"]
  K1 = Relay [part_number=FRS1B-S package=THT]
  S2 = Pushbutton [package="[THT]"]
  D3 = Zener Diode [part_number=1N4732A breakdown_voltage=3.6V package="Melf DO-213 AB [SMD]"]

nets:
  N1: DIN1.3, Composant1.D6_PWM
  N2: DIN1.2, K1.B, D3.cathode
  N3: J1.pin2, C1.+
  N4: Composant1.A3, Q1.gate
  N5: Composant1.A4/SDA, IC1.SDA_-_I2C_Data
  N6: Composant1.A5/SCL, IC1.SCL_-_I2C_Clock
  N7: Composant1.GND, Q1.source, K1.COIL1, S2.Pin_4
  N8: Composant1.D7, S2.Pin_1, S2.Pin_2
  N9: IC1.X1_-_Crystal, XTAL1.pin_0
  N10: IC1.X2_-_Crystal, XTAL1.pin_1
  N11: IC1.Vbat_-_Backup_Supply, BAT1.-
  N12: IC1.0V, BAT1.+
  N13: R1.Pin_1, R2.Pin_1
  N14: Q1.drain, K1.COIL2
  N15: K1.A, D3.anode
  N16: K1.C1, K1.C2
